# Fritzing sketch dispThermoHygroMeter (saved by Fritzing 0.9.3b)
breadboards: 1

parts:
  Raspberry_Pi_1 = Raspberry Pi 3 [part_number=RPI-3-V1.2]
  OLED_I2C1 = OLED 128x64 I2C Monochrome Display
  DHT11_1 = DHT11 module

nets:
  3V3: Raspberry_Pi_1.3v3, Raspberry_Pi_1.3V3, OLED_I2C1.VDD, DHT11_1.DATA
  N1: Raspberry_Pi_1.GPIO2, OLED_I2C1.SDA
  N2: Raspberry_Pi_1.GPIO3, OLED_I2C1.SCK
  GND: Raspberry_Pi_1.GND, OLED_I2C1.GND, DHT11_1.GND
  N3: Raspberry_Pi_1.GPIO14, DHT11_1.VCC

custom parts:
  DHT11 module: DHT11 black pcb module
